// Logisim project main.circ as structural Verilog: 4 circuits, main circuit main
module main (
  input  a,
  output x
);

  Transistor transistor_1 (.in(1'b1), .out(x), .gate(a));
  Transistor transistor_2 (.in(1'b0), .out(x), .gate(a));
endmodule

module \and  (
  input  a,
  output x
);

  Transistor transistor_1 (.in(1'b1), .out(x), .gate(a));
  Transistor transistor_2 (.in(1'b0), .out(x), .gate(a));
endmodule

module \or  (
  input  X,
  input  Y,
  output x_2
);

  Transistor transistor_1 (.in(1'b1), .out(x_2), .gate(X));
  Transistor transistor_2 (.in(1'b0), .out(x_2), .gate(Y));
endmodule

module \not  (
  input  X,
  output out_2
);

  wire transistor_2_out;

  Transistor transistor_1 (.in(1'b1), .out(out_2), .gate(X));
  Transistor transistor_2 (.in(out_2), .out(transistor_2_out), .gate(X));
  // also tied to GND on the sheet: transistor_2_out
endmodule
